// Logisim project SingleCycleCore.circ as structural Verilog: 11 circuits, main circuit RVI 1cycle
module RVI_1cycle (
);

  wire alu_1_zero, ALUSrc, and_1_out, Branch, Clk, MemRead, MemtoReg, MemWrite, RegWrite,
       Reset_Program_Counter_out, Reset_Regs_out;
  wire [1:0] ALUOp;
  wire [3:0] alu_control_1_out_4;
  wire [6:0] InstControl;
  wire [7:0] alu_1_result_2;
  wire [31:0] adder_1_out, adder_2_out, alu_1_result, immgen_1_immediate, multiplexer_1_out,
       multiplexer_2_out, multiplexer_3_out, PC_q, ram_1_data, register_file_1_readdata1,
       register_file_1_readdata2;
  wire [31:7] rom_1_data;

  Clock clock_1 (.out(Clk));
  Register #(.width(32)) PC (.D(multiplexer_2_out), .Q(PC_q), .clk(Clk), .clr(Reset_Program_Counter_out));  // open: en
  Button Reset_Program_Counter (.out(Reset_Program_Counter_out));
  Adder #(.width(32)) adder_1 (.a(32'h4), .b(PC_q), .out(adder_1_out));  // open: cin, cout
  Main_Control main_control_1 (
    .Instruction(InstControl), .ALUSrc(ALUSrc), .MemtoReg(MemtoReg), .RegWrite(RegWrite), .MemRead(MemRead),
    .MemWrite(MemWrite), .Branch(Branch), .ALUOp(ALUOp));
  ROM #(.dataWidth(32)) rom_1 (.addr(PC_q[9:2]), .data({rom_1_data, InstControl}));  // open: sel
  Button Reset_Regs (.out(Reset_Regs_out));
  ImmGen immgen_1 (.Instruction({rom_1_data, InstControl}), .Immediate(immgen_1_immediate));
  // Probe on rom_1_data[30]
  // Probe on rom_1_data[14:12]
  Register_File register_file_1 (
    .Clk(Clk), .Rst(Reset_Regs_out), .ReadData1(register_file_1_readdata1),
    .ReadData2(register_file_1_readdata2), .WriteEn(RegWrite), .WriteDir(rom_1_data[11:7]),
    .WriteData(multiplexer_3_out), .ReadDir1(rom_1_data[19:15]), .ReadDir2(rom_1_data[24:20]));
  // Probe on register_file_1_readdata1
  // Probe on register_file_1_readdata2
  // Probe on immgen_1_immediate
  ALU_Control alu_control_1 (
    .out_4(alu_control_1_out_4), .ALUOp(ALUOp), .Func7(rom_1_data[30]), .Func3(rom_1_data[14:12]));
  // Probe on ALUOp
  Adder #(.width(32)) adder_2 (.a(PC_q), .b(immgen_1_immediate), .out(adder_2_out));  // open: cin, cout
  Multiplexer #(.width(32), .enable("false")) multiplexer_1 (
    .in0(register_file_1_readdata2), .in1(immgen_1_immediate), .out(multiplexer_1_out), .sel(ALUSrc));
  // Probe on multiplexer_1_out
  ALU alu_1 (
    .Result({alu_1_result[31:10], alu_1_result_2, alu_1_result[1:0]}), .Zero(alu_1_zero),
    .a(register_file_1_readdata1), .b(multiplexer_1_out), .Alu_Operation(alu_control_1_out_4));
  // Probe on alu_control_1_out_4
  Multiplexer #(.width(32), .enable("false")) multiplexer_2 (
    .in0(adder_1_out), .in1(adder_2_out), .out(multiplexer_2_out), .sel(and_1_out));
  and and_1 (and_1_out, Branch, alu_1_zero);
  // Probe on {alu_1_result[31:10], alu_1_result_2, alu_1_result[1:0]}
  RAM #(.dataWidth(32), .bus("separate")) ram_1 (
    .addr(alu_1_result_2), .din(register_file_1_readdata2), .data(ram_1_data), .str(MemWrite), .clk(Clk),
    .ld(MemRead));  // open: sel, clr
  // Probe on multiplexer_3_out
  // Probe on ram_1_data
  Multiplexer #(.width(32), .enable("false")) multiplexer_3 (
    .in0({alu_1_result[31:10], alu_1_result_2, alu_1_result[1:0]}), .in1(ram_1_data),
    .out(multiplexer_3_out), .sel(MemtoReg));

  // Notes on the sheet:
  //   Alineado a word (1:0 = 0)
  //   contents of rom_1 (hex, n*v repeats v):
  //   52503 85a583 a58633 c2a423 2b60063 40b606b3 40d60633 b60a63 4*0 c6f6b3 c6e733
  //   Alineado a word (1:0 = 0)
endmodule

module Main_Control (
  input  [6:0] Instruction,
  output ALUSrc,
  output MemtoReg,
  output RegWrite,
  output MemRead,
  output MemWrite,
  output Branch,
  output [1:0] ALUOp
);

  and R (ALUOp[1], ~Instruction[6], Instruction[5], Instruction[4], ~Instruction[3], ~Instruction[2], Instruction[1], Instruction[0]);  // AND_Gate
  and lw (MemRead, ~Instruction[6], ~Instruction[5], ~Instruction[4], ~Instruction[3], ~Instruction[2], Instruction[1], Instruction[0]);  // AND_Gate
  and sw (MemWrite, ~Instruction[6], Instruction[5], ~Instruction[4], ~Instruction[3], ~Instruction[2], Instruction[1], Instruction[0]);  // AND_Gate
  and beq (ALUOp[0], Instruction[6], Instruction[5], ~Instruction[4], ~Instruction[3], ~Instruction[2], Instruction[1], Instruction[0]);  // AND_Gate
  or or_1 (ALUSrc, MemRead, MemWrite);
  or or_2 (RegWrite, ALUOp[1], MemRead);

  assign Branch = ALUOp[0];
  assign MemtoReg = MemRead;
endmodule

module Register_File (
  input  [4:0] ReadDir1,
  input  [4:0] ReadDir2,
  input  WriteEn,
  input  [4:0] WriteDir,
  input  [31:0] WriteData,
  input  Clk,
  input  Rst,
  output [31:0] ReadData1,
  output [31:0] ReadData2
);

  wire [15:0] decoder_1_out0, decoder_1_out16;
  wire [31:0] x1___ra_q, x2___sp_q, x3___gp_q, x4___tp_q, x5___t0_q, x6___t1_q, x7___t2_q, x8___s0___fp_q,
       x9___s1_q, x10___a0_q, x11___a1_q, x12___a2_q, x13___a3_q, x14___a4_q, x15___a5_q, x16___a6_q,
       x17___a7_q, x18___s2_q, x19___s3_q, x20___s4_q, x21___s5_q, x22___s6_q, x23___s7_q, x24___s8_q,
       x25___s9_q, x26___s10_q, x27___s11_q, x28___t3_q, x29___t4_q, x30___t5_q, x31___t6_q;

  Decoder #(.select(5), .disabled(0)) decoder_1 (
    .out0(decoder_1_out0[0]), .out1(decoder_1_out0[1]), .out2(decoder_1_out0[2]), .out3(decoder_1_out0[3]),
    .out4(decoder_1_out0[4]), .out5(decoder_1_out0[5]), .out6(decoder_1_out0[6]), .out7(decoder_1_out0[7]),
    .out8(decoder_1_out0[8]), .out9(decoder_1_out0[9]), .out10(decoder_1_out0[10]),
    .out11(decoder_1_out0[11]), .out12(decoder_1_out0[12]), .out13(decoder_1_out0[13]),
    .out14(decoder_1_out0[14]), .out15(decoder_1_out0[15]), .out16(decoder_1_out16[0]),
    .out17(decoder_1_out16[1]), .out18(decoder_1_out16[2]), .out19(decoder_1_out16[3]),
    .out20(decoder_1_out16[4]), .out21(decoder_1_out16[5]), .out22(decoder_1_out16[6]),
    .out23(decoder_1_out16[7]), .out24(decoder_1_out16[8]), .out25(decoder_1_out16[9]),
    .out26(decoder_1_out16[10]), .out27(decoder_1_out16[11]), .out28(decoder_1_out16[12]),
    .out29(decoder_1_out16[13]), .out30(decoder_1_out16[14]), .out31(decoder_1_out16[15]), .sel(WriteDir),
    .en(WriteEn));
  // Probe on decoder_1_out0
  // Probe on WriteDir
  Register #(.width(32)) x1___ra (.D(WriteData), .en(decoder_1_out0[1]), .Q(x1___ra_q), .clk(Clk), .clr(Rst));
  Register #(.width(32)) x2___sp (.D(WriteData), .en(decoder_1_out0[2]), .Q(x2___sp_q), .clk(Clk), .clr(Rst));
  Register #(.width(32)) x3___gp (.D(WriteData), .en(decoder_1_out0[3]), .Q(x3___gp_q), .clk(Clk), .clr(Rst));
  Register #(.width(32)) x4___tp (.D(WriteData), .en(decoder_1_out0[4]), .Q(x4___tp_q), .clk(Clk), .clr(Rst));
  Register #(.width(32)) x5___t0 (.D(WriteData), .en(decoder_1_out0[5]), .Q(x5___t0_q), .clk(Clk), .clr(Rst));
  Register #(.width(32)) x6___t1 (.D(WriteData), .en(decoder_1_out0[6]), .Q(x6___t1_q), .clk(Clk), .clr(Rst));
  Register #(.width(32)) x7___t2 (.D(WriteData), .en(decoder_1_out0[7]), .Q(x7___t2_q), .clk(Clk), .clr(Rst));
  Register #(.width(32)) x8___s0___fp (.D(WriteData), .en(decoder_1_out0[8]), .Q(x8___s0___fp_q), .clk(Clk), .clr(Rst));
  Register #(.width(32)) x9___s1 (.D(WriteData), .en(decoder_1_out0[9]), .Q(x9___s1_q), .clk(Clk), .clr(Rst));
  Register #(.width(32)) x10___a0 (.D(WriteData), .en(decoder_1_out0[10]), .Q(x10___a0_q), .clk(Clk), .clr(Rst));
  Register #(.width(32)) x11___a1 (.D(WriteData), .en(decoder_1_out0[11]), .Q(x11___a1_q), .clk(Clk), .clr(Rst));
  Register #(.width(32)) x12___a2 (.D(WriteData), .en(decoder_1_out0[12]), .Q(x12___a2_q), .clk(Clk), .clr(Rst));
  Register #(.width(32)) x13___a3 (.D(WriteData), .en(decoder_1_out0[13]), .Q(x13___a3_q), .clk(Clk), .clr(Rst));
  Register #(.width(32)) x14___a4 (.D(WriteData), .en(decoder_1_out0[14]), .Q(x14___a4_q), .clk(Clk), .clr(Rst));
  Register #(.width(32)) x15___a5 (.D(WriteData), .en(decoder_1_out0[15]), .Q(x15___a5_q), .clk(Clk), .clr(Rst));
  // Probe on x13___a3_q
  Register #(.width(32)) x16___a6 (.D(WriteData), .en(decoder_1_out16[0]), .Q(x16___a6_q), .clk(Clk), .clr(Rst));
  Register #(.width(32)) x17___a7 (.D(WriteData), .en(decoder_1_out16[1]), .Q(x17___a7_q), .clk(Clk), .clr(Rst));
  Register #(.width(32)) x18___s2 (.D(WriteData), .en(decoder_1_out16[2]), .Q(x18___s2_q), .clk(Clk), .clr(Rst));
  Register #(.width(32)) x19___s3 (.D(WriteData), .en(decoder_1_out16[3]), .Q(x19___s3_q), .clk(Clk), .clr(Rst));
  Register #(.width(32)) x20___s4 (.D(WriteData), .en(decoder_1_out16[4]), .Q(x20___s4_q), .clk(Clk), .clr(Rst));
  Register #(.width(32)) x21___s5 (.D(WriteData), .en(decoder_1_out16[5]), .Q(x21___s5_q), .clk(Clk), .clr(Rst));
  Register #(.width(32)) x22___s6 (.D(WriteData), .en(decoder_1_out16[6]), .Q(x22___s6_q), .clk(Clk), .clr(Rst));
  Register #(.width(32)) x23___s7 (.D(WriteData), .en(decoder_1_out16[7]), .Q(x23___s7_q), .clk(Clk), .clr(Rst));
  Register #(.width(32)) x24___s8 (.D(WriteData), .en(decoder_1_out16[8]), .Q(x24___s8_q), .clk(Clk), .clr(Rst));
  Register #(.width(32)) x25___s9 (.D(WriteData), .en(decoder_1_out16[9]), .Q(x25___s9_q), .clk(Clk), .clr(Rst));
  Register #(.width(32)) x26___s10 (.D(WriteData), .en(decoder_1_out16[10]), .Q(x26___s10_q), .clk(Clk), .clr(Rst));
  Register #(.width(32)) x27___s11 (.D(WriteData), .en(decoder_1_out16[11]), .Q(x27___s11_q), .clk(Clk), .clr(Rst));
  Register #(.width(32)) x28___t3 (.D(WriteData), .en(decoder_1_out16[12]), .Q(x28___t3_q), .clk(Clk), .clr(Rst));
  Register #(.width(32)) x29___t4 (.D(WriteData), .en(decoder_1_out16[13]), .Q(x29___t4_q), .clk(Clk), .clr(Rst));
  Register #(.width(32)) x30___t5 (.D(WriteData), .en(decoder_1_out16[14]), .Q(x30___t5_q), .clk(Clk), .clr(Rst));
  Register #(.width(32)) x31___t6 (.D(WriteData), .en(decoder_1_out16[15]), .Q(x31___t6_q), .clk(Clk), .clr(Rst));
  Multiplexer #(.select(5), .width(32), .enable("false")) multiplexer_1 (
    .in0({32{1'b0}}), .in1(x1___ra_q), .in2(x2___sp_q), .in3(x3___gp_q), .in4(x4___tp_q), .in5(x5___t0_q),
    .in6(x6___t1_q), .in7(x7___t2_q), .in8(x8___s0___fp_q), .in9(x9___s1_q), .in10(x10___a0_q),
    .in11(x11___a1_q), .in12(x12___a2_q), .in13(x13___a3_q), .in14(x14___a4_q), .in15(x15___a5_q),
    .in16(x16___a6_q), .in17(x17___a7_q), .in18(x18___s2_q), .in19(x19___s3_q), .in20(x20___s4_q),
    .in21(x21___s5_q), .in22(x22___s6_q), .in23(x23___s7_q), .in24(x24___s8_q), .in25(x25___s9_q),
    .in26(x26___s10_q), .in27(x27___s11_q), .in28(x28___t3_q), .in29(x29___t4_q), .in30(x30___t5_q),
    .in31(x31___t6_q), .out(ReadData1), .sel(ReadDir1));
  Multiplexer #(.select(5), .width(32), .enable("false")) multiplexer_2 (
    .in0({32{1'b0}}), .in1(x1___ra_q), .in2(x2___sp_q), .in3(x3___gp_q), .in4(x4___tp_q), .in5(x5___t0_q),
    .in6(x6___t1_q), .in7(x7___t2_q), .in8(x8___s0___fp_q), .in9(x9___s1_q), .in10(x10___a0_q),
    .in11(x11___a1_q), .in12(x12___a2_q), .in13(x13___a3_q), .in14(x14___a4_q), .in15(x15___a5_q),
    .in16(x16___a6_q), .in17(x17___a7_q), .in18(x18___s2_q), .in19(x19___s3_q), .in20(x20___s4_q),
    .in21(x21___s5_q), .in22(x22___s6_q), .in23(x23___s7_q), .in24(x24___s8_q), .in25(x25___s9_q),
    .in26(x26___s10_q), .in27(x27___s11_q), .in28(x28___t3_q), .in29(x29___t4_q), .in30(x30___t5_q),
    .in31(x31___t6_q), .out(ReadData2), .sel(ReadDir2));

  // Notes on the sheet:
  //   WriteReg
  //   If not not-floating,
  //   when disabled, it can lead to
  //   write all regs
  //   x0 - zero
endmodule

module ALU_Control (
  input  [1:0] ALUOp,
  input  Func7,
  input  [2:0] Func3,
  output [3:0] out_4
);

  wire add_out, and_out, beq_out, lw_out, or_out, sub_out, sw_out, undriven_3;
  wire [1:0] undriven;
  wire [2:0] alucontroltabletocircuit_1_alu2, undriven_2;

  and lw (lw_out, ~ALUOp[1], ~ALUOp[0]);  // AND_Gate
  ALUControlTableToCircuit alucontroltabletocircuit_1 (
    .ALUOp1(undriven[1]), .ALUOp0(undriven[0]), .i30(undriven_3), .i14(undriven_2[2]), .i13(undriven_2[1]),
    .i12(undriven_2[0]), .ALU2(alucontroltabletocircuit_1_alu2[0]),
    .ALU1(alucontroltabletocircuit_1_alu2[1]), .ALU0(alucontroltabletocircuit_1_alu2[2]));
  and sw (sw_out, ~ALUOp[1], ~ALUOp[0]);  // AND_Gate
  and beq (beq_out, ~ALUOp[1], ALUOp[0]);  // AND_Gate
  and add (add_out, ALUOp[1], ~ALUOp[0], ~Func7, ~Func3[2], ~Func3[1], ~Func3[0]);  // AND_Gate
  and sub (sub_out, ALUOp[1], ~ALUOp[0], Func7, ~Func3[2], ~Func3[1], ~Func3[0]);  // AND_Gate
  and \and  (and_out, ALUOp[1], ~ALUOp[0], ~Func7, Func3[2], Func3[1], Func3[0]);  // AND_Gate
  and \or  (or_out, ALUOp[1], ~ALUOp[0], ~Func7, Func3[2], Func3[1], ~Func3[0]);  // AND_Gate
  buf or_2 (out_4[0], or_out);  // OR_Gate
  or or_3 (out_4[1], lw_out, sw_out, beq_out, add_out, sub_out);
  or or_4 (out_4[2], beq_out, sub_out);
  // OR_Gate or_5 is placed but not wired

  assign out_4[3] = 1'b0;
endmodule

module ALU (
  input  [3:0] Alu_Operation,
  input  [31:0] a,
  input  [31:0] b,
  output [31:0] Result,
  output Zero
);

  wire n1bit_alu_1_cout, n1bit_alu_2_cout, n1bit_alu_3_cout, n1bit_alu_4_cout, n1bit_alu_5_cout,
       n1bit_alu_6_cout, n1bit_alu_7_cout, n1bit_alu_8_cout, n1bit_alu_9_cout, n1bit_alu_10_cout,
       n1bit_alu_11_cout, n1bit_alu_12_cout, n1bit_alu_13_cout, n1bit_alu_14_cout, n1bit_alu_15_cout,
       n1bit_alu_16_cout, n1bit_alu_17_cout, n1bit_alu_18_cout, n1bit_alu_19_cout, n1bit_alu_20_cout,
       n1bit_alu_21_cout, n1bit_alu_22_cout, n1bit_alu_23_cout, n1bit_alu_24_cout, n1bit_alu_25_cout,
       n1bit_alu_26_cout, n1bit_alu_27_cout, n1bit_alu_28_cout, n1bit_alu_29_cout, n1bit_alu_30_cout,
       n1bit_alu_31_1_set, n1bit_alu_31_cout, or_1_out, Result29;

  _1bit_ALU u_1bit_alu_1 (
    .a(a[0]), .b(b[0]), .cin(Alu_Operation[2]), .Less(n1bit_alu_31_1_set), .cout(n1bit_alu_1_cout),
    .Result(Result[0]), .Ainvert(Alu_Operation[3]), .Binvert(Alu_Operation[2]), .in_3(Alu_Operation[1:0]));
  _1bit_ALU u_1bit_alu_2 (
    .a(a[1]), .b(b[1]), .cin(n1bit_alu_1_cout), .Less(1'b0), .cout(n1bit_alu_2_cout), .Result(Result[1]),
    .Ainvert(Alu_Operation[3]), .Binvert(Alu_Operation[2]), .in_3(Alu_Operation[1:0]));
  _1bit_ALU u_1bit_alu_3 (
    .a(a[2]), .b(b[2]), .cin(n1bit_alu_2_cout), .Less(1'b0), .cout(n1bit_alu_3_cout), .Result(Result[2]),
    .Ainvert(Alu_Operation[3]), .Binvert(Alu_Operation[2]), .in_3(Alu_Operation[1:0]));
  _1bit_ALU u_1bit_alu_4 (
    .a(a[3]), .b(b[3]), .cin(n1bit_alu_3_cout), .Less(1'b0), .cout(n1bit_alu_4_cout), .Result(Result[3]),
    .Ainvert(Alu_Operation[3]), .Binvert(Alu_Operation[2]), .in_3(Alu_Operation[1:0]));
  _1bit_ALU u_1bit_alu_5 (
    .a(a[4]), .b(b[4]), .cin(n1bit_alu_4_cout), .Less(1'b0), .cout(n1bit_alu_5_cout), .Result(Result[4]),
    .Ainvert(Alu_Operation[3]), .Binvert(Alu_Operation[2]), .in_3(Alu_Operation[1:0]));
  _1bit_ALU u_1bit_alu_6 (
    .a(a[5]), .b(b[5]), .cin(n1bit_alu_5_cout), .Less(1'b0), .cout(n1bit_alu_6_cout), .Result(Result[5]),
    .Ainvert(Alu_Operation[3]), .Binvert(Alu_Operation[2]), .in_3(Alu_Operation[1:0]));
  _1bit_ALU u_1bit_alu_7 (
    .a(a[6]), .b(b[6]), .cin(n1bit_alu_6_cout), .Less(1'b0), .cout(n1bit_alu_7_cout), .Result(Result[6]),
    .Ainvert(Alu_Operation[3]), .Binvert(Alu_Operation[2]), .in_3(Alu_Operation[1:0]));
  _1bit_ALU u_1bit_alu_8 (
    .a(a[7]), .b(b[7]), .cin(n1bit_alu_7_cout), .Less(1'b0), .cout(n1bit_alu_8_cout), .Result(Result[7]),
    .Ainvert(Alu_Operation[3]), .Binvert(Alu_Operation[2]), .in_3(Alu_Operation[1:0]));
  _1bit_ALU u_1bit_alu_9 (
    .a(a[8]), .b(b[8]), .cin(n1bit_alu_8_cout), .Less(1'b0), .cout(n1bit_alu_9_cout), .Result(Result[8]),
    .Ainvert(Alu_Operation[3]), .Binvert(Alu_Operation[2]), .in_3(Alu_Operation[1:0]));
  _1bit_ALU u_1bit_alu_10 (
    .a(a[9]), .b(b[9]), .cin(n1bit_alu_9_cout), .Less(1'b0), .cout(n1bit_alu_10_cout), .Result(Result[9]),
    .Ainvert(Alu_Operation[3]), .Binvert(Alu_Operation[2]), .in_3(Alu_Operation[1:0]));
  _1bit_ALU u_1bit_alu_11 (
    .a(a[10]), .b(b[10]), .cin(n1bit_alu_10_cout), .Less(1'b0), .cout(n1bit_alu_11_cout),
    .Result(Result[10]), .Ainvert(Alu_Operation[3]), .Binvert(Alu_Operation[2]), .in_3(Alu_Operation[1:0]));
  _1bit_ALU u_1bit_alu_12 (
    .a(a[11]), .b(b[11]), .cin(n1bit_alu_11_cout), .Less(1'b0), .cout(n1bit_alu_12_cout),
    .Result(Result[11]), .Ainvert(Alu_Operation[3]), .Binvert(Alu_Operation[2]), .in_3(Alu_Operation[1:0]));
  _1bit_ALU u_1bit_alu_13 (
    .a(a[12]), .b(b[12]), .cin(n1bit_alu_12_cout), .Less(1'b0), .cout(n1bit_alu_13_cout),
    .Result(Result[12]), .Ainvert(Alu_Operation[3]), .Binvert(Alu_Operation[2]), .in_3(Alu_Operation[1:0]));
  _1bit_ALU u_1bit_alu_14 (
    .a(a[13]), .b(b[13]), .cin(n1bit_alu_13_cout), .Less(1'b0), .cout(n1bit_alu_14_cout),
    .Result(Result[13]), .Ainvert(Alu_Operation[3]), .Binvert(Alu_Operation[2]), .in_3(Alu_Operation[1:0]));
  _1bit_ALU u_1bit_alu_15 (
    .a(a[14]), .b(b[14]), .cin(n1bit_alu_14_cout), .Less(1'b0), .cout(n1bit_alu_15_cout),
    .Result(Result[14]), .Ainvert(Alu_Operation[3]), .Binvert(Alu_Operation[2]), .in_3(Alu_Operation[1:0]));
  _1bit_ALU u_1bit_alu_16 (
    .a(a[15]), .b(b[15]), .cin(n1bit_alu_15_cout), .Less(1'b0), .cout(n1bit_alu_16_cout),
    .Result(Result[15]), .Ainvert(Alu_Operation[3]), .Binvert(Alu_Operation[2]), .in_3(Alu_Operation[1:0]));
  _1bit_ALU u_1bit_alu_17 (
    .a(a[16]), .b(b[16]), .cin(n1bit_alu_16_cout), .Less(1'b0), .cout(n1bit_alu_17_cout),
    .Result(Result[16]), .Ainvert(Alu_Operation[3]), .Binvert(Alu_Operation[2]), .in_3(Alu_Operation[1:0]));
  _1bit_ALU u_1bit_alu_18 (
    .a(a[17]), .b(b[17]), .cin(n1bit_alu_17_cout), .Less(1'b0), .cout(n1bit_alu_18_cout),
    .Result(Result[17]), .Ainvert(Alu_Operation[3]), .Binvert(Alu_Operation[2]), .in_3(Alu_Operation[1:0]));
  _1bit_ALU u_1bit_alu_19 (
    .a(a[18]), .b(b[18]), .cin(n1bit_alu_18_cout), .Less(1'b0), .cout(n1bit_alu_19_cout),
    .Result(Result[18]), .Ainvert(Alu_Operation[3]), .Binvert(Alu_Operation[2]), .in_3(Alu_Operation[1:0]));
  _1bit_ALU u_1bit_alu_20 (
    .a(a[19]), .b(b[19]), .cin(n1bit_alu_19_cout), .Less(1'b0), .cout(n1bit_alu_20_cout),
    .Result(Result[19]), .Ainvert(Alu_Operation[3]), .Binvert(Alu_Operation[2]), .in_3(Alu_Operation[1:0]));
  _1bit_ALU u_1bit_alu_21 (
    .a(a[20]), .b(b[20]), .cin(n1bit_alu_20_cout), .Less(1'b0), .cout(n1bit_alu_21_cout),
    .Result(Result[20]), .Ainvert(Alu_Operation[3]), .Binvert(Alu_Operation[2]), .in_3(Alu_Operation[1:0]));
  _1bit_ALU u_1bit_alu_22 (
    .a(a[21]), .b(b[21]), .cin(n1bit_alu_21_cout), .Less(1'b0), .cout(n1bit_alu_22_cout),
    .Result(Result[21]), .Ainvert(Alu_Operation[3]), .Binvert(Alu_Operation[2]), .in_3(Alu_Operation[1:0]));
  _1bit_ALU u_1bit_alu_23 (
    .a(a[22]), .b(b[22]), .cin(n1bit_alu_22_cout), .Less(1'b0), .cout(n1bit_alu_23_cout),
    .Result(Result[22]), .Ainvert(Alu_Operation[3]), .Binvert(Alu_Operation[2]), .in_3(Alu_Operation[1:0]));
  _1bit_ALU u_1bit_alu_24 (
    .a(a[23]), .b(b[23]), .cin(n1bit_alu_23_cout), .Less(1'b0), .cout(n1bit_alu_24_cout),
    .Result(Result[23]), .Ainvert(Alu_Operation[3]), .Binvert(Alu_Operation[2]), .in_3(Alu_Operation[1:0]));
  _1bit_ALU u_1bit_alu_25 (
    .a(a[24]), .b(b[24]), .cin(n1bit_alu_24_cout), .Less(1'b0), .cout(n1bit_alu_25_cout),
    .Result(Result[24]), .Ainvert(Alu_Operation[3]), .Binvert(Alu_Operation[2]), .in_3(Alu_Operation[1:0]));
  _1bit_ALU u_1bit_alu_26 (
    .a(a[25]), .b(b[25]), .cin(n1bit_alu_25_cout), .Less(1'b0), .cout(n1bit_alu_26_cout),
    .Result(Result[25]), .Ainvert(Alu_Operation[3]), .Binvert(Alu_Operation[2]), .in_3(Alu_Operation[1:0]));
  _1bit_ALU u_1bit_alu_27 (
    .a(a[26]), .b(b[26]), .cin(n1bit_alu_26_cout), .Less(1'b0), .cout(n1bit_alu_27_cout),
    .Result(Result[26]), .Ainvert(Alu_Operation[3]), .Binvert(Alu_Operation[2]), .in_3(Alu_Operation[1:0]));
  _1bit_ALU u_1bit_alu_28 (
    .a(a[27]), .b(b[27]), .cin(n1bit_alu_27_cout), .Less(1'b0), .cout(n1bit_alu_28_cout),
    .Result(Result[27]), .Ainvert(Alu_Operation[3]), .Binvert(Alu_Operation[2]), .in_3(Alu_Operation[1:0]));
  _1bit_ALU u_1bit_alu_29 (
    .a(a[28]), .b(b[28]), .cin(n1bit_alu_28_cout), .Less(1'b0), .cout(n1bit_alu_29_cout),
    .Result(Result[29]), .Ainvert(Alu_Operation[3]), .Binvert(Alu_Operation[2]), .in_3(Alu_Operation[1:0]));
  _1bit_ALU u_1bit_alu_30 (
    .a(a[29]), .b(b[29]), .cin(n1bit_alu_29_cout), .Less(1'b0), .cout(n1bit_alu_30_cout), .Result(Result29),
    .Ainvert(Alu_Operation[3]), .Binvert(Alu_Operation[2]), .in_3(Alu_Operation[1:0]));
  _1bit_ALU u_1bit_alu_31 (
    .a(a[30]), .b(b[30]), .cin(n1bit_alu_30_cout), .Less(1'b0), .cout(n1bit_alu_31_cout),
    .Result(Result[30]), .Ainvert(Alu_Operation[3]), .Binvert(Alu_Operation[2]), .in_3(Alu_Operation[1:0]));
  _1bit_ALU_31 u_1bit_alu_31_1 (
    .a(a[31]), .b(b[31]), .cin(n1bit_alu_31_cout), .Less(1'b0), .Set(n1bit_alu_31_1_set),
    .Result(Result[31]), .Ainvert(Alu_Operation[3]), .Binvert(Alu_Operation[2]), .in_3(Alu_Operation[1:0]));  // open: cout
  not not_1 (Zero, or_1_out);
  or or_1 (or_1_out, Result[0], Result[1], Result[2], Result[3], Result[4], Result[5], Result[6], Result[7], Result[8], Result[9], Result[10], Result[11], Result[12], Result[13], Result[14], Result[15], Result[16], Result[17], Result[18], Result[19], Result[20], Result[21], Result[22], Result[23], Result[24], Result[25], Result[26], Result[27], Result[29], Result[29], Result[30], Result[31]);

  assign Result[28] = Result[29];

  // Other names for the same wires on the sheet: Op[1:0] = Alu_Operation[1:0]; Binv = Alu_Operation[2];
  //   Ainv = Alu_Operation[3]; Result28 = Result[29]

  // Notes on the sheet:
  //   Binv in cin1 to sub
endmodule

module _1bit_ALU (
  input  Ainvert,
  input  Binvert,
  input  [1:0] in_3,
  input  a,
  input  b,
  input  cin,
  input  Less,
  output cout,
  output Result
);

  wire _0, _1, _2, multiplexer_1_out, multiplexer_2_out, not_1_out, not_2_out;

  not not_1 (not_1_out, a);
  not not_2 (not_2_out, b);
  Multiplexer #(.enable("false")) multiplexer_1 (.in0(a), .in1(not_1_out), .out(multiplexer_1_out), .sel(Ainvert));
  Multiplexer #(.enable("false")) multiplexer_2 (.in0(b), .in1(not_2_out), .out(multiplexer_2_out), .sel(Binvert));
  and and_1 (_0, multiplexer_1_out, multiplexer_2_out);
  or or_1 (_1, multiplexer_1_out, multiplexer_2_out);
  _1bit_Adder u_1bit_adder_1 (
    .Sum_2(_2), .cout_2(cout), .a_2(multiplexer_1_out), .b_2(multiplexer_2_out), .cin_2(cin));  // open: sum, cout, a, b, cin
  Multiplexer #(.select(2), .enable("false")) multiplexer_3 (
    .in0(_0), .in1(_1), .in2(_2), .in3(Less), .out(Result), .sel(in_3));

  // Other names for the same wires on the sheet: _3 = Less
endmodule

module _1bit_ALU_31 (
  input  Ainvert,
  input  Binvert,
  input  [1:0] in_3,
  input  a,
  input  b,
  input  cin,
  input  Less,
  output Set,
  output cout,
  output Result
);

  wire _0, _1, multiplexer_1_out, multiplexer_2_out, not_1_out, not_2_out;

  not not_1 (not_1_out, a);
  not not_2 (not_2_out, b);
  Multiplexer #(.enable("false")) multiplexer_1 (.in0(a), .in1(not_1_out), .out(multiplexer_1_out), .sel(Ainvert));
  Multiplexer #(.enable("false")) multiplexer_2 (.in0(b), .in1(not_2_out), .out(multiplexer_2_out), .sel(Binvert));
  and and_1 (_0, multiplexer_1_out, multiplexer_2_out);
  or or_1 (_1, multiplexer_1_out, multiplexer_2_out);
  _1bit_Adder u_1bit_adder_1 (
    .Sum_2(Set), .cout_2(cout), .a_2(multiplexer_1_out), .b_2(multiplexer_2_out), .cin_2(cin));  // open: sum, cout, a, b, cin
  Multiplexer #(.select(2), .enable("false")) multiplexer_3 (
    .in0(_0), .in1(_1), .in2(Set), .in3(Less), .out(Result), .sel(in_3));

  // Other names for the same wires on the sheet: _2 = Set; _3 = Less
endmodule

module _1bit_Adder (
  input  a,
  input  b,
  input  cin,
  input  a_2,
  input  b_2,
  input  cin_2,
  output sum,
  output Sum_2,
  output cout,
  output cout_2
);

  wire and_1_out, and_2_out, and_3_out, and_4_out, and_5_out, and_6_out, and_7_out, and_8_out, and_9_out,
       and_10_out;

  and and_1 (and_1_out, a_2, ~b_2, ~cin_2);  // AND_Gate
  and and_2 (and_2_out, ~a_2, b_2, ~cin_2);  // AND_Gate
  and and_3 (and_3_out, ~a_2, ~b_2, cin_2);  // AND_Gate
  and and_4 (and_4_out, a_2, b_2, cin_2);
  and and_5 (and_5_out, a_2, cin_2);
  and and_6 (and_6_out, b_2, cin_2);
  and and_7 (and_7_out, a_2, b_2);
  or or_1 (Sum_2, and_1_out, and_2_out, and_3_out, and_4_out);
  or or_2 (cout_2, and_5_out, and_6_out, and_7_out);
  ExactlyOne xor_1 (.out(sum), .in0(a), .in1(b), .in2(cin));
  and and_8 (and_8_out, a, cin);
  and and_9 (and_9_out, b, cin);
  and and_10 (and_10_out, a, b);
  or or_3 (cout, and_8_out, and_9_out, and_10_out);

  // Notes on the sheet:
  //   Basic configuration using AND & OR
  //   The choice between this 2 types of adder depends on the technology used to implement it. 
  //   XOR configuration
  //   Using the carrier out directly seems faster than dividing the 3XOR in 2 parts XOR
endmodule

module ImmGen (
  input  [31:0] Instruction,
  output [31:0] Immediate
);

  wire [31:0] bit_extender_1_out, Btype, Itype, Jtype, shifter_1_out, Stype, undriven;

  Bit_Extender #(.in_width(20), .out_width(32), .\type ("sign")) bit_extender_1 (.out(bit_extender_1_out));  // open: in
  Shifter #(.width(32)) shifter_1 (.in(bit_extender_1_out), .\dist (5'b01100), .out(shifter_1_out));
  assign Stype = {{20{Instruction[31]}}, {Instruction[31:25], Instruction[11:7]}};  // Bit_Extender bit_extender_2
  assign Btype = {{19{Instruction[31]}}, {Instruction[31], Instruction[7], Instruction[30:25], Instruction[11:8], 1'b0}};  // Bit_Extender bit_extender_3
  assign Jtype = {{11{Instruction[31]}}, {Instruction[31], Instruction[19:12], Instruction[20], Instruction[30:21], 1'b0}};  // Bit_Extender bit_extender_4
  assign Itype = {{21{Instruction[31]}}, Instruction[31:21]};  // Bit_Extender bit_extender_5
  // Probe on Stype
  // Probe on Btype
  // Probe on {Instruction[31:12], {12{1'b0}}}
  // Probe on Jtype
  // Probe on Itype
  Multiplexer #(.select(5), .width(32), .enable("false")) multiplexer_1 (
    .in0(Itype), .in3(undriven), .in4(undriven), .in5({Instruction[31:12], {12{1'b0}}}), .in8(Stype),
    .in13({Instruction[31:12], {12{1'b0}}}), .in24(Btype), .in25(undriven), .in27(Jtype), .in28(undriven),
    .out(Immediate), .sel(Instruction[6:2]));  // open: in1, in2, in6, in7, in9, in10, in11, in12, in14, in15, in16, in17, in18, in19, in20, in21, in22, in23, in26, in29, in30, in31
  // Probe on Instruction[6:2]

  // Other names for the same wires on the sheet: Utype[31:12] = Instruction[31:12]

  // Notes on the sheet:
  //   "Sign Extend" [19:0] = 0
  //   Calculate all posibilities of immediates and select one of them based on opcode
  //   Use control lines to implement what of the immediates is being to be generated
  //   From this 2 options the second one seems to increment the complexity of the desing while the first one don't implicitly reduces its performance
  //   Bits 2-6 of opcode
  //   Loads
  //   fence
  //   Arithmetics
  //   aupic
  //   Stores
  //   lui
  //   Branches
  //   jalr
  //   jal
  //   ecall/ebreak
endmodule

module ImmGen32Mux (
  input  [31:0] Instruction,
  input  [31:0] Result
);

  wire o29, undriven, undriven_2;

  Multiplexer #(.enable("false")) multiplexer_1 (.out(Result[0]), .sel(undriven));  // open: in0, in1
  Multiplexer #(.enable("false")) multiplexer_2 (.out(Result[1]), .sel(undriven));  // open: in0, in1
  Multiplexer #(.enable("false")) multiplexer_3 (.out(Result[2]), .sel(undriven));  // open: in0, in1
  Multiplexer #(.enable("false")) multiplexer_4 (.out(Result[3]), .sel(undriven));  // open: in0, in1
  Multiplexer #(.enable("false")) multiplexer_5 (.out(Result[4]), .sel(undriven));  // open: in0, in1
  Multiplexer #(.enable("false")) multiplexer_6 (.out(Result[5]), .sel(undriven));  // open: in0, in1
  Multiplexer #(.enable("false")) multiplexer_7 (.out(Result[6]), .sel(undriven));  // open: in0, in1
  Multiplexer #(.enable("false")) multiplexer_8 (.out(Result[7]), .sel(undriven));  // open: in0, in1
  Multiplexer #(.enable("false")) multiplexer_9 (.out(Result[8]), .sel(undriven));  // open: in0, in1
  Multiplexer #(.enable("false")) multiplexer_10 (.out(Result[9]), .sel(undriven));  // open: in0, in1
  Multiplexer #(.enable("false")) multiplexer_11 (.out(Result[10]), .sel(undriven));  // open: in0, in1
  Multiplexer #(.enable("false")) multiplexer_12 (.out(Result[11]), .sel(undriven));  // open: in0, in1
  Multiplexer #(.enable("false")) multiplexer_13 (.out(Result[12]), .sel(undriven));  // open: in0, in1
  Multiplexer #(.enable("false")) multiplexer_14 (.out(Result[13]), .sel(undriven));  // open: in0, in1
  Multiplexer #(.enable("false")) multiplexer_15 (.out(Result[14]), .sel(undriven));  // open: in0, in1
  Multiplexer #(.enable("false")) multiplexer_16 (.out(Result[15]), .sel(undriven));  // open: in0, in1
  Multiplexer #(.enable("false")) multiplexer_17 (.out(Result[16]), .sel(undriven_2));  // open: in0, in1
  Multiplexer #(.enable("false")) multiplexer_18 (.out(Result[17]), .sel(undriven_2));  // open: in0, in1
  Multiplexer #(.enable("false")) multiplexer_19 (.out(Result[18]), .sel(undriven_2));  // open: in0, in1
  Multiplexer #(.enable("false")) multiplexer_20 (.out(Result[19]), .sel(undriven_2));  // open: in0, in1
  Multiplexer #(.enable("false")) multiplexer_21 (.out(Result[20]), .sel(undriven_2));  // open: in0, in1
  Multiplexer #(.enable("false")) multiplexer_22 (.out(Result[21]), .sel(undriven_2));  // open: in0, in1
  Multiplexer #(.enable("false")) multiplexer_23 (.out(Result[22]), .sel(undriven_2));  // open: in0, in1
  Multiplexer #(.enable("false")) multiplexer_24 (.out(Result[23]), .sel(undriven_2));  // open: in0, in1
  Multiplexer #(.enable("false")) multiplexer_25 (.out(Result[24]), .sel(undriven_2));  // open: in0, in1
  Multiplexer #(.enable("false")) multiplexer_26 (.out(Result[25]), .sel(undriven_2));  // open: in0, in1
  Multiplexer #(.enable("false")) multiplexer_27 (.out(Result[26]), .sel(undriven_2));  // open: in0, in1
  Multiplexer #(.enable("false")) multiplexer_28 (.out(Result[27]), .sel(undriven_2));  // open: in0, in1
  Multiplexer #(.enable("false")) multiplexer_29 (.out(Result[29]), .sel(undriven_2));  // open: in0, in1
  Multiplexer #(.enable("false")) multiplexer_30 (.out(o29), .sel(undriven_2));  // open: in0, in1
  Multiplexer #(.enable("false")) multiplexer_31 (
    .in0(Instruction[31]), .in1(Instruction[30]), .out(Result[30]), .sel(undriven_2));

  assign {Result[31], Result[28]} = {Instruction[31], Result[29]};

  // Other names for the same wires on the sheet: i0 = Instruction[0]; i1 = Instruction[1]; i2 = Instruction[2];
  //   i3 = Instruction[3]; i4 = Instruction[4]; i5 = Instruction[5]; i6 = Instruction[6]; i7 = Instruction[7];
  //   i8 = Instruction[8]; i9 = Instruction[9]; i10 = Instruction[10]; i11 = Instruction[11]; i12 = Instruction[12];
  //   i13 = Instruction[13]; i14 = Instruction[14]; i15 = Instruction[15]; i16 = Instruction[16];
  //   i17 = Instruction[17]; i18 = Instruction[18]; i19 = Instruction[19]; i20 = Instruction[20];
  //   i21 = Instruction[21]; i22 = Instruction[22]; i23 = Instruction[23]; i24 = Instruction[24];
  //   i25 = Instruction[25]; i26 = Instruction[26]; i27 = Instruction[27]; i28 = Instruction[28];
  //   i29 = Instruction[29]; i30 = Instruction[30]; o0 = Result[0]; o1 = Result[1]; o2 = Result[2]; o3 = Result[3];
  //   o4 = Result[4]; o5 = Result[5]; o6 = Result[6]; o7 = Result[7]; o8 = Result[8]; o9 = Result[9];
  //   o10 = Result[10]; o11 = Result[11]; o12 = Result[12]; o13 = Result[13]; o14 = Result[14]; o15 = Result[15];
  //   o16 = Result[16]; o17 = Result[17]; o18 = Result[18]; o19 = Result[19]; o20 = Result[20]; o21 = Result[21];
  //   o22 = Result[22]; o23 = Result[23]; o24 = Result[24]; o25 = Result[25]; o26 = Result[26]; o27 = Result[27];
  //   o28 = Result[29]; o30 = Result[30]; i31 = Instruction[31]; o31 = Instruction[31]

  // Notes on the sheet:
  //   Implementation of the ImmGen following Figure 4.18, from which decuces that every out bit has its own MUX and ?is selected by a control line?
endmodule

module ALUControlTableToCircuit (
  input  ALUOp1,
  input  ALUOp0,
  input  i30,
  input  i14,
  input  i13,
  input  i12,
  output ALU2,
  output ALU1,
  output ALU0
);

  wire not_1_out, not_2_out, not_3_out, not_4_out;

  not not_1 (not_1_out, ALUOp1);
  not not_2 (not_2_out, i14);
  not not_3 (not_3_out, ALUOp1);
  not not_4 (not_4_out, i14);
  not not_5 (ALU0, i12);
  or or_1 (ALU2, not_1_out, not_2_out);
  or or_2 (ALU1, not_3_out, not_4_out);
endmodule
